// Logisim project pierre-feuille-ciseau.circ as structural Verilog: 1 circuit, main circuit main
module main (
  input  a,
  input  b,
  input  c,
  input  d,
  output L1,
  output L2
);

  wire a_b_cd_out, a_bc_out, ac_d_out, acd_out, b_cd_out, bcd_out, minus_abc_d_out, minus_abd_out, not_1_out,
       not_2_out, not_3_out, not_4_out, not_5_out, not_6_out, not_7_out, not_8_out;

  and acd (acd_out, a, c, d);
  and a_bc (a_bc_out, a, not_1_out, c);
  not not_1 (not_1_out, b);
  not not_2 (not_2_out, a);
  and minus_abc_d (minus_abc_d_out, not_2_out, b, not_3_out, c);
  not not_3 (not_3_out, d);
  and b_cd (b_cd_out, b, not_4_out, d);
  not not_4 (not_4_out, c);
  not not_5 (not_5_out, a);
  and minus_abd (minus_abd_out, not_5_out, b, d);
  and ac_d (ac_d_out, a, c, not_6_out);
  not not_6 (not_6_out, d);
  and bcd (bcd_out, b, c, d);
  not not_7 (not_7_out, b);
  and a_b_cd (a_b_cd_out, a, not_7_out, not_8_out, d);
  not not_8 (not_8_out, c);
  or or_1 (L1, acd_out, a_bc_out, minus_abc_d_out, b_cd_out);
  or or_2 (L2, minus_abd_out, ac_d_out, bcd_out, a_b_cd_out);
endmodule
